# Fritzing sketch barbot (saved by Fritzing 0.9.2b)
breadboards: 1

parts:
  Part1 = Arduino Nano (Rev3.0)
  M1 = Stepper Motor - Bipolar
  Power_plug1 = Power plug
  DRV1 = A4983
  J1 = Basic Servo
  U1 = Voltage Regulator - 5V [package="TO220 [THT]"]

nets:
  GND: Part1.GND, DRV1.GND, J1.gnd
  N1: Part1.D8, DRV1.EN
  N2: Part1.D10, J1.pulse
  N3: Part1.D11/MOSI, DRV1.STEP
  N4: Part1.D12/MISO, DRV1.DIR
  5V: Part1.5V, DRV1.MS1, DRV1.MS2, DRV1.MS3, DRV1.VDD
  N5: M1.A, DRV1.2B
  N6: M1.C, DRV1.2A
  N7: M1.B, DRV1.1A
  N8: M1.D, DRV1.1B
  GND_2: Power_plug1.GND, DRV1.GNDMOT, U1.GND
  N9: Power_plug1.VCC, DRV1.VMOT, U1.input_voltage
  N10: DRV1.RST, DRV1.SLP
  N11: J1.vcc, U1.output_voltage

custom parts:
  A4983: Poloko A4983 Stepper Motor Control Breakout
